# Fritzing sketch Multivibrator_astable (saved by Fritzing 0.9.3b)
breadboards: 1

parts:
  R1 = Resistor [tolerance=±5% resistance=200 package="1206 [SMD]"]
  LED2 = smd LED [color="Red (633nm)" package="0603 [SMD]"]
  LED1 = smd LED [color="Green (555nm)" package="0603 [SMD]"]
  R4 = Resistor [tolerance=±5% resistance=200 package="1206 [SMD]"]
  BAT1 = Battery Holders [package=battcom_20mm_pth]
  C1 = Electrolytic Capacitor [capacitance=100µF voltage=50V package="200 mil [THT, electrolytic]"]
  R2 = Resistor [tolerance=±5% resistance=10k package="1206 [SMD]"]
  C2 = Electrolytic Capacitor [capacitance=100µF voltage=50V package="200 mil [THT, electrolytic]"]
  R3 = Resistor [tolerance=±5% resistance=10k package="1206 [SMD]"]
  Q1 = NPN-Transistor [part_number=bc547 package="TO92 [THT]"]
  Q2 = NPN-Transistor [part_number=bc547 package="TO92 [THT]"]

nets:
  N1: R1.Pin_0, LED1.anode
  N2: R1.Pin_1, R4.Pin_0, BAT1.-, R2.Pin_0, R3.Pin_1
  N3: LED2.cathode, C2.+, Q2.C
  N4: LED2.anode, R4.Pin_1
  N5: LED1.cathode, C1.+, Q1.C
  N6: BAT1.+, Q1.E, Q2.E
  N7: C1.-, R2.Pin_1, Q2.B
  N8: C2.-, R3.Pin_0, Q1.B
