# Fritzing sketch Multivibrator_astable_DC_motor (saved by Fritzing 0.9.3b)
breadboards: 1

parts:
  R1 = Resistor [tolerance=±5% resistance=200 package="1206 [SMD]"]
  LED2 = smd LED [color="Red (633nm)" package="0603 [SMD]"]
  LED1 = smd LED [color="Green (555nm)" package="0603 [SMD]"]
  R4 = Resistor [tolerance=±5% resistance=200 package="1206 [SMD]"]
  BAT1 = Battery Holders [package=battcom_20mm_pth]
  C1 = Electrolytic Capacitor [capacitance=1µF voltage=50V package="200 mil [THT, electrolytic]"]
  R2 = Resistor [tolerance=±5% resistance=10k package="1206 [SMD]"]
  C2 = Electrolytic Capacitor [capacitance=1µF voltage=50V package="200 mil [THT, electrolytic]"]
  R3 = Resistor [tolerance=±5% resistance=10k package="1206 [SMD]"]
  Q1 = NPN-Transistor [part_number=bc547 package="TO92 [THT]"]
  Q2 = NPN-Transistor [part_number=bc547 package="TO92 [THT]"]
  R5 = Rotary Potentiometer (Large) [maximum_resistance=50kΩ package=THT]
  R6 = Resistor [tolerance=±5% resistance=200 package="1206 [SMD]"]
  Q3 = MOSFET-NCHANNEL [package=to-92]
  M1 = DC Motor

nets:
  N1: R1.Pin_0, LED1.anode
  N2: R1.Pin_1, R4.Pin_0, BAT1.-, R5.wiper, M1.pin_1
  N3: LED2.cathode, C2.+, Q2.C, R6.Pin_1
  N4: LED2.anode, R4.Pin_1
  N5: LED1.cathode, C1.+, Q1.C
  N6: BAT1.+, Q1.E, Q2.E, Q3.S
  N7: C1.-, R2.Pin_1, Q2.B
  N8: R2.Pin_0, R5.leg1
  N9: C2.-, R3.Pin_0, Q1.B
  N10: R3.Pin_1, R5.leg2
  N11: R6.Pin_0, Q3.G
  N12: Q3.D, M1.pin_2
